# Fritzing sketch Gizmo_board2 (saved by Fritzing 0.9.3b)
circuit board: 6.86cm x 5.35cm

parts:
  IR_RECEIVE2 = LED - 5mm [color="Blue (430nm)" package="5 mm [THT]"]
  IR_RECEIVE1 = LED - 5mm [color="Blue (430nm)" package="5 mm [THT]"]
  R1 = Resistor [tolerance=±5% resistance=180 package="0805 [SMD]"]
  R2 = Resistor [tolerance=±5% resistance=180 package="0805 [SMD]"]
  180 = Resistor [tolerance=±5% resistance=100 package="0805 [SMD]"]
  180_2 = Resistor [tolerance=±5% resistance=100 package="0805 [SMD]"]
  47K = Resistor [tolerance=±5% resistance=47k package="0805 [SMD]"]
  BLUETOOTH = Bluetooth HC-05 Macho
  RGB_LED = Header 4 [package=molex-1x4_lock]
  74HC139N2 = 74HC139N [part_number=74HC139N package="DIP (Dual Inline) [THT]"]
  R3 = Resistor [tolerance=±5% resistance=180 package="0805 [SMD]"]
  ULN2803A = ULN2803A [package=THT]
  IR_EMIT2 = LED - 5mm [color="Infrared (940nm)" package="5 mm [THT]"]
  47K_2 = Resistor [tolerance=±0.05% resistance=47k package="0805 [SMD]"]
  STEPPER2 = male alternating pin header, 5 pins [form="♂ (male)"]
  STEPPER1 = male alternating pin header, 5 pins [form="♂ (male)"]
  SWITCH = SPST Switch [package=switch-spdt_kit]
  V_MOTOR = Header 2 [package=screwterminal-3.5mm-2_lock]
  V_BATT = Header 2 [package=screwterminal-3.5mm-2_lock]
  C3 = Ceramic Capacitor [capacitance=1µF package="0805 [SMD, multilayer]"]
  C4 = Ceramic Capacitor [capacitance=1µF package="0805 [SMD, multilayer]"]
  ARDUINO = Arduino Nano (Rev3.0)
  IR_EMIT1 = LED - 5mm [color="Infrared (940nm)" package="5 mm [THT]"]
  ULTRA_DIST = Header 4 [package=molex-1x4_lock]

nets:
  VCC: IR_RECEIVE2.cathode, IR_RECEIVE1.cathode, 180.Pin_1, 180_2.Pin_1, 47K.Pin_0, BLUETOOTH.VCC, RGB_LED.2, 74HC139N2.VCC, 47K_2.Pin_0, C4.1, ARDUINO.5V, ULTRA_DIST.1
  GND: IR_RECEIVE2.anode, IR_RECEIVE1.anode, BLUETOOTH.GND, 74HC139N2.GND, ULN2803A.0V, IR_EMIT2.cathode, V_MOTOR.2, V_BATT.2, C3.0, C4.0, ARDUINO.GND, IR_EMIT1.cathode, ULTRA_DIST.4
  N1: R1.Pin_0, ARDUINO.D11/MOSI
  N2: R1.Pin_1, RGB_LED.4
  N3: R2.Pin_0, ARDUINO.D10
  N4: R2.Pin_1, RGB_LED.3
  N5: 180.Pin_0, IR_EMIT1.anode
  N6: 180_2.Pin_0, IR_EMIT2.anode
  N7: 47K.Pin_1, ARDUINO.A1
  N8: BLUETOOTH.TXD, ARDUINO.D1/TX
  N9: BLUETOOTH.RXD, ARDUINO.D0/RX
  N10: RGB_LED.1, R3.Pin_1
  N11: 74HC139N2.1G_, 74HC139N2.2G_, ARDUINO.D12/MISO
  N12: 74HC139N2.1A, ARDUINO.D8
  N13: 74HC139N2.1B, ARDUINO.D7
  N14: 74HC139N2.1Y0, ULN2803A.In_4
  N15: 74HC139N2.1Y1, ULN2803A.In_3
  N16: 74HC139N2.1Y2, ULN2803A.In_2
  N17: 74HC139N2.1Y3, ULN2803A.In_1
  N18: 74HC139N2.2Y3, ULN2803A.In_8
  N19: 74HC139N2.2Y2, ULN2803A.In_7
  N20: 74HC139N2.2Y1, ULN2803A.In_6
  N21: 74HC139N2.2Y0, ULN2803A.In_5
  N22: 74HC139N2.2B, ARDUINO.D4
  N23: 74HC139N2.2A, ARDUINO.D5
  N24: R3.Pin_0, ARDUINO.D9
  N25: ULN2803A.COM_-_Common, STEPPER2.pin1, STEPPER1.pin1, V_MOTOR.1, C3.1
  N26: ULN2803A.Out_8, STEPPER2.pin2
  N27: ULN2803A.Out_7, STEPPER2.pin3
  N28: ULN2803A.Out_6, STEPPER2.pin4
  N29: ULN2803A.Out_5, STEPPER2.pin5
  N30: ULN2803A.Out_4, STEPPER1.pin2
  N31: ULN2803A.Out_3, STEPPER1.pin3
  N32: ULN2803A.Out_2, STEPPER1.pin4
  N33: ULN2803A.Out_1, STEPPER1.pin5
  N34: 47K_2.Pin_1, ARDUINO.A0
  N35: SWITCH.O, V_BATT.1
  N36: SWITCH.P, ARDUINO.VIN
  N37: ARDUINO.D2, ULTRA_DIST.2
  N38: ARDUINO.D3, ULTRA_DIST.3

notes:
  Do not connect red wires on stepper motors
