# Fritzing sketch Gizmo_breadboard (saved by Fritzing 0.9.3b)
breadboards: 1

parts:
  Part1 = Arduino Nano (Rev3.0)
  LED1 = RGB LED - (4 legs) [package="5 mm [THT]"]
  J1 = Basic Servo
  M2 = Stepper Motor - Bipolar
  IC1 = L293D [package=THT]
  S1 = SPST Switch [package=switch-spdt_kit]
  Part2 = Bluetooth HC-05 Macho
  IC2 = L293D [package=THT]
  IR_EMIT2 = LED - 5mm [color="Infrared (940nm)" package="5 mm [THT]"]
  IR_RECEIVE2 = LED - 5mm [color="Blue (430nm)" package="5 mm [THT]"]
  IR_RECEIVE1 = LED - 5mm [color="Blue (430nm)" package="5 mm [THT]"]
  IR_EMIT1 = LED - 5mm [color="Infrared (940nm)" package="5 mm [THT]"]
  HC-SR04_Sensor_1 = HC-SR04 Ultrasonic Distance Sensor
  V_MOTOR = Battery Holders [package=battcon_245mm]
  R1 = Resistor [tolerance=±5% resistance=100 package="0805 [SMD]"]
  R2 = Resistor [tolerance=±5% resistance=100 package="0805 [SMD]"]
  R3 = Resistor [tolerance=±5% resistance=180 package="0805 [SMD]"]
  V_BATT = Battery Holders [package=battcon_245mm]
  R4 = Resistor [tolerance=±5% resistance=180 package="0805 [SMD]"]
  R5 = Resistor [tolerance=±5% resistance=47k package="0805 [SMD]"]
  R6 = Resistor [tolerance=±5% resistance=180 package="0805 [SMD]"]
  R7 = Resistor [tolerance=±5% resistance=47k package="0805 [SMD]"]
  M1 = Stepper Motor - Bipolar
  CD4555B1 = CD4555B [part_number=CD4555B package="DIP (Dual Inline) [THT]"]

nets (from the breadboard view):
  N1: Part1.D1/TX, Part2.TXD
  N2: Part1.D0/RX, Part2.RXD
  GND: Part1.GND, J1.gnd, IC1.Enable_1, IC1.0V, IC1.Enable_2, Part2.GND, IC2.Enable_1, IC2.0V, IC2.Enable_2, IR_EMIT2.cathode, IR_RECEIVE2.anode, IR_RECEIVE1.anode, IR_EMIT1.cathode, HC-SR04_Sensor_1.GND, V_MOTOR.-, V_BATT.-
  N3: Part1.D2, HC-SR04_Sensor_1.TRIG
  N4: Part1.D3, HC-SR04_Sensor_1.ECHO
  N5: Part1.D4, CD4555B1.1G_, CD4555B1.2G_
  N6: Part1.D6, J1.pulse
  N7: Part1.D7, CD4555B1.1A
  N8: Part1.D8, CD4555B1.1B
  N9: Part1.D9, R3.Pin_0
  N10: Part1.D10, R2.Pin_0
  N11: Part1.D11/MOSI, R1.Pin_0
  N12: Part1.D12/MISO, CD4555B1.2A
  N13: Part1.VIN, S1.P
  VCC: Part1.5V, LED1.common_anode, Part2.VCC, IR_RECEIVE2.cathode, IR_RECEIVE1.cathode, HC-SR04_Sensor_1.VCC, R4.Pin_1, R5.Pin_0, R6.Pin_1, R7.Pin_0, CD4555B1.Vss, CD4555B1.VCC
  N14: Part1.A1, R5.Pin_1
  N15: Part1.A0, R7.Pin_1
  N16: Part1.D13/SCK, CD4555B1.2B
  N17: LED1.red_cathode, R3.Pin_1
  N18: LED1.green_cathode, R2.Pin_1
  N19: LED1.blue_cathode, R1.Pin_1
  N20: J1.vcc, IC1.+Vmotor, IC1.+V, IC2.+Vmotor, IC2.+V, V_MOTOR.+
  N21: M2.A, IC1.Out_1_(_Controlled_by_Enable_1_)
  N22: M2.C, IC1.Out_2_(_Controlled_by_Enable_1_)
  N23: M2.B, IC1.Out_3_(_Controlled_by_Enable_2_)
  N24: M2.D, IC1.Out_4_(_Controlled_by_Enable_2_)
  N25: IC1.In_1, CD4555B1.1Y0
  N26: IC1.In_2, CD4555B1.1Y1
  N27: IC1.In_3, CD4555B1.1Y2
  N28: IC1.In_4, CD4555B1.1Y3
  N29: S1.O, V_BATT.+
  N30: IC2.In_1, CD4555B1.2Y0
  N31: IC2.Out_1_(_Controlled_by_Enable_1_), M1.A
  N32: IC2.Out_2_(_Controlled_by_Enable_1_), M1.C
  N33: IC2.In_2, CD4555B1.2Y1
  N34: IC2.In_3, CD4555B1.2Y2
  N35: IC2.Out_3_(_Controlled_by_Enable_2_), M1.B
  N36: IC2.Out_4_(_Controlled_by_Enable_2_), M1.D
  N37: IC2.In_4, CD4555B1.2Y3
  N38: IR_EMIT2.anode, R6.Pin_0
  N39: IR_EMIT1.anode, R4.Pin_0

notes:
  Do not connect red wires on stepper motors

custom parts:
  CD4555B: A Dual 2 to 4 DEMX / Decoder
